// Logisim project Logisim.circ as structural Verilog: 7 circuits, main circuit main
module main (
  input  PA,
  input  PP_DR,
  input  MO,
  input  LK,
  input  Reset,
  output BOLT,
  output BOLT_2,
  output L2M,
  output R2M,
  output M2L,
  output M2R
);

  wire and_1_out, Counter_out_4, Counter_out_5;

  door_circuit door_circuit_1 (
    .PA(PA), .PP(PP_DR), .MO(MO), .LK(LK), .reset(Reset), .BOLT(BOLT), .R2M_L2M(L2M), .M2R_M2L(M2L));
  door_circuit door_circuit_2 (
    .PA(PA), .PP(PP_DR), .MO(MO), .LK(LK), .reset(Reset), .BOLT(BOLT_2), .R2M_L2M(R2M), .M2R_M2L(M2R));
  counter Counter (.MO(MO), .BOLT(BOLT_2), .Reset(Reset), .out_4(Counter_out_4), .out_5(Counter_out_5));
  and and_1 (and_1_out, Counter_out_4, Counter_out_5);
  // Simple_buzzer simple_buzzer_1: pin names not known; wires that end beside it: and_1_out

  // Notes on the sheet:
  //   INPUTS
  //   PA = Person Approaching Sensor
  //   MO = Manual Open/Remote Control
  //   LK = Door Lock
  //   NOTE:
  //   Doors take a few seconds to close/open
  //   automatic doors
  //   Left Door
  //   comparable to actual commerical
  //   Buzzer can be stopped only on reseting the circuit
  //   Left-door-circuit
  //   PP = Person Presence Sensor(person present in door frame) or Door Resistance
  //   AUTOMATIC DOOR CONTROLLER
  //   Right-door-circuit
  //   BOLT = Door is locked
  //   Right Door
  //   OUTPUTS
  //   R2M = Motor closes the right door
  //   M2R = Motor opens the right door
  //   L2M = Motor closes the left door
  //   M2L = Motor opens the left door
  //   Buzzer = Alarm to warn 3 failed manual attempts when door is bolted
  //   ALARM
endmodule

module output_module (
  input  PA,
  input  PP,
  input  MO,
  input  Y1_t,
  input  Y2_t,
  input  R_L,
  input  M,
  input  LK,
  output BOLT,
  output R2M_L2M,
  output M2R_M2L
);

  wire and_1_out, and_3_out, not_1_out, not_2_out, not_3_out, not_4_out, not_5_out, not_6_out, or_1_out,
       or_2_out, or_3_out;

  or or_1 (or_1_out, PA, PP, MO);
  not not_1 (not_1_out, or_1_out);
  not not_2 (not_2_out, Y1_t);
  not not_3 (not_3_out, Y2_t);
  not not_4 (not_4_out, R_L);
  not not_5 (not_5_out, M);
  not not_6 (not_6_out, LK);
  and and_1 (and_1_out, or_1_out, not_4_out);
  and and_2 (BOLT, not_2_out, not_3_out, LK);
  and and_3 (and_3_out, not_1_out, not_5_out, not_6_out);
  or or_2 (or_2_out, and_1_out, not_2_out);
  and and_4 (M2R_M2L, or_2_out, Y2_t);
  or or_3 (or_3_out, and_3_out, Y1_t);
  and and_5 (R2M_L2M, or_3_out, not_3_out);

  // Notes on the sheet:
  //   INPUTS
  //   Y1,Y2 = Present State
  //   R/L = Door completely open
  //   M = Door completely close
  //   OUTPUTS
  //   BOLT = Door Locked
  //   R2M/L2M = Motor closes the door
  //   M2R/M2L = Motor opens the door
  //   Output Circuit Module
endmodule

module \output  (
  input  [7:0] Inputs,
  output [2:0] Outputs
);

  output_module Output_Circuit_Module (
    .PA(Inputs[7]), .PP(Inputs[6]), .MO(Inputs[5]), .Y1_t(Inputs[4]), .Y2_t(Inputs[3]), .R_L(Inputs[2]),
    .M(Inputs[1]), .LK(Inputs[0]), .BOLT(Outputs[0]), .R2M_L2M(Outputs[1]), .M2R_M2L(Outputs[2]));

  // Notes on the sheet:
  //   Concepts Used:
  //   Analysis of sequential circuits used
  //   OUTPUT CIRCUIT
  //   Steps:
  //   1) State Diagram was drawn based on self analysis of doors used in commercials.
  //   2) State Table was drawn, and output equations were simplified with the help of K-maps.
endmodule

module nextstate_module (
  input  PA,
  input  PP,
  input  MO,
  input  Y1_t,
  input  Y2_t,
  input  R_L,
  input  M,
  input  LK,
  output Y1_t_1,
  output Y2_t_1
);

  wire and_1_out, and_2_out, and_3_out, and_4_out, and_5_out, and_6_out, and_7_out, not_1_out, not_2_out,
       not_3_out, not_4_out, not_5_out, not_6_out, or_1_out;

  or or_1 (or_1_out, PA, PP, MO);
  not not_1 (not_1_out, or_1_out);
  not not_2 (not_2_out, Y1_t);
  not not_3 (not_3_out, Y2_t);
  not not_4 (not_4_out, R_L);
  not not_5 (not_5_out, M);
  not not_6 (not_6_out, LK);
  and and_1 (and_1_out, not_2_out, Y2_t, R_L);
  and and_2 (and_2_out, Y1_t, Y2_t);
  and and_3 (and_3_out, Y1_t, not_3_out, not_5_out, not_1_out);
  and and_4 (and_4_out, not_2_out, not_3_out, not_6_out, or_1_out);
  and and_5 (and_5_out, not_2_out, Y2_t);
  and and_6 (and_6_out, Y1_t, Y2_t, or_1_out);
  and and_7 (and_7_out, or_1_out, not_3_out, Y1_t);
  or or_2 (Y1_t_1, and_1_out, and_2_out, and_3_out);
  or or_3 (Y2_t_1, and_4_out, and_5_out, and_6_out, and_7_out);

  // Notes on the sheet:
  //   NEXTSTATE CIRCUIT MODULE
  //   OUTPUTS
  //   Y1(t+1), Y2(t+1) = Next State
endmodule

module nextstate (
  input  [1:0] current_state,
  input  [5:0] Input,
  output [1:0] next_state
);

  nextstate_module nextstate_module (
    .PA(Input[5]), .PP(Input[4]), .MO(Input[3]), .Y1_t(current_state[1]), .Y2_t(current_state[0]),
    .R_L(Input[2]), .M(Input[1]), .LK(Input[0]), .Y1_t_1(next_state[1]), .Y2_t_1(next_state[0]));

  // Notes on the sheet:
  //   CONCEPTS USED:
  //   State of Door
  //   Closed(Reset)
  //   Opening
  //   Opened
  //   Closing
  //   State assignment was used to denote the four states of the door :
  //   Next State equations were found using K-maps
  //   Assignment
  //   00
  //   01
  //   11
  //   10
  //   NEXTSTATE CIRCUIT
endmodule

module door_circuit (
  input  PA,
  input  PP,
  input  MO,
  input  LK,
  input  reset,
  output BOLT,
  output R2M_L2M,
  output M2R_M2L
);

  wire Clock_2_out, Clock_out, not_1_out, or_1_out;
  wire [1:0] d_ff_1_q, NextState_next_state;
  wire [2:1] M_q;

  Clock #(.highDuration(2), .lowDuration(2)) Clock (.out(Clock_out));
  or or_1 (or_1_out, MO, PP, PA);
  not not_1 (not_1_out, or_1_out);
  Clock Clock_2 (.out(Clock_2_out));
  D_Flip_Flop R_L (.clk(Clock_out), .D(or_1_out), .Q(M_q[2]));  // open: Qn, preset, en, reset
  D_Flip_Flop M (.clk(Clock_out), .D(not_1_out), .Q(M_q[1]));  // open: Qn, preset, en, reset
  nextstate NextState (.Input({PA, PP, MO, M_q, LK}), .current_state(d_ff_1_q), .next_state(NextState_next_state));
  D_Flip_Flop d_ff_1 (
    .clk(Clock_2_out), .D(NextState_next_state[0]), .Q(d_ff_1_q[0]), .preset(reset));  // open: Qn, en, reset
  D_Flip_Flop d_ff_2 (
    .clk(Clock_2_out), .D(NextState_next_state[1]), .Q(d_ff_1_q[1]), .preset(reset));  // open: Qn, en, reset
  \output  Output (.Inputs({PA, PP, MO, d_ff_1_q, M_q, LK}), .Outputs({M2R_M2L, R2M_L2M, BOLT}));

  // Notes on the sheet:
  //   DOOR CIRCUIT
endmodule

module counter (
  input  MO,
  input  BOLT,
  input  Reset,
  output out_4,
  output out_5
);

  wire and_1_out, nand_1_out;

  T_Flip_Flop t_ff_1 (.clk(MO), .T(nand_1_out), .Q(out_5), .preset(and_1_out), .reset(Reset), .en(BOLT));  // open: Qn
  nand nand_1 (nand_1_out, out_5, out_4);
  and and_1 (and_1_out, out_5, out_4);
  T_Flip_Flop t_ff_2 (.clk(MO), .T(out_5), .Q(out_4), .preset(and_1_out), .reset(Reset), .en(BOLT));  // open: Qn

  // Notes on the sheet:
  //   2 BIT Counter
endmodule
